# Fritzing sketch ipoverserial (saved by Fritzing 0.9.4)
breadboards: 1

parts:
  RPi-a = Raspberry Pi Zero
  RPi-b = Raspberry Pi Zero

nets:
  N1: RPi-a.pin_6, RPi-a.pin_9, RPi-b.pin_6, RPi-b.pin_34, RPi-b.pin_39
  N2: RPi-a.pin_8, RPi-b.pin_10
  N3: RPi-a.pin_10, RPi-b.pin_8
