# Fritzing sketch ipviaarduino (saved by Fritzing 0.9.4)
breadboards: 1

parts:
  RPi-a = Raspberry Pi Zero
  RPi-b = Raspberry Pi Zero
  Arduino_Mega_2560 = Arduino Mega 2560 (Rev3)
  BSS138_Logic_Level_Converter = Adafruit 4-channel I2C-safe Bi-directional Logic Level Converter [part_number="Adafruit #757"]

nets:
  N1: RPi-a.pin_1, BSS138_Logic_Level_Converter.LV
  GND: RPi-a.pin_6, RPi-b.pin_6, RPi-b.pin_39, Arduino_Mega_2560.GND, BSS138_Logic_Level_Converter.GND
  N2: RPi-a.pin_8, BSS138_Logic_Level_Converter.A2
  N3: RPi-a.pin_10, BSS138_Logic_Level_Converter.A1
  N4: RPi-b.pin_8, BSS138_Logic_Level_Converter.A4
  N5: RPi-b.pin_10, BSS138_Logic_Level_Converter.A3
  N6: Arduino_Mega_2560.D17_PWM/RX2, BSS138_Logic_Level_Converter.B4
  N7: Arduino_Mega_2560.D16_PWM/TX2, BSS138_Logic_Level_Converter.B3
  N8: Arduino_Mega_2560.D15/RX3, BSS138_Logic_Level_Converter.B2
  N9: Arduino_Mega_2560.D14/TX3, BSS138_Logic_Level_Converter.B1
  N10: Arduino_Mega_2560.5V, BSS138_Logic_Level_Converter.HV

custom parts:
  Adafruit 4-channel I2C-safe Bi-directional Logic Level Converter: Because the Arduino (and Basic Stamp) are 5V devices, and most modern sensors, displays, flash cards and modes are 3.3V-only, many makers find that they need to perform level shifting/conversion to protect the 3.3V device from 5V. We do have some other handy level shifters in the shop, from the DIP 74LVC245 to the fancy bi-directional TXB0108. However, neither of these are happy to work with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
