# Fritzing sketch ipviaradio (saved by Fritzing 0.9.4)
breadboards: 1

parts:
  RPi-a_/_RPi-b = Raspberry Pi Zero
  Arduino_Mega_2560 = Arduino Mega 2560 (Rev3)
  BSS138_Logic_Level_Converter = Adafruit 4-channel I2C-safe Bi-directional Logic Level Converter [part_number="Adafruit #757"]
  Radio_-_RFM95W = Adafruit RFM9x LoRa Radio [part_number="Adafruit #3072 and #3073"]

nets:
  N1: RPi-a_/_RPi-b.pin_1, BSS138_Logic_Level_Converter.LV
  GND: RPi-a_/_RPi-b.pin_6, RPi-a_/_RPi-b.pin_9, Arduino_Mega_2560.GND, BSS138_Logic_Level_Converter.GND, Radio_-_RFM95W.GND
  N2: RPi-a_/_RPi-b.pin_8, BSS138_Logic_Level_Converter.A2
  N3: RPi-a_/_RPi-b.pin_10, BSS138_Logic_Level_Converter.A1
  N4: Arduino_Mega_2560.D15/RX3, BSS138_Logic_Level_Converter.B2
  N5: Arduino_Mega_2560.D14/TX3, BSS138_Logic_Level_Converter.B1
  5V: Arduino_Mega_2560.5V, BSS138_Logic_Level_Converter.HV, Radio_-_RFM95W.VIN
  N6: Arduino_Mega_2560.D2_PWM, Radio_-_RFM95W.RST
  N7: Arduino_Mega_2560.D3_PWM, Radio_-_RFM95W.DIO0
  N8: Arduino_Mega_2560.D4_PWM, Radio_-_RFM95W.CS
  N9: Arduino_Mega_2560.D50, Radio_-_RFM95W.MISO
  N10: Arduino_Mega_2560.D51, Radio_-_RFM95W.MOSI
  N11: Arduino_Mega_2560.D52, Radio_-_RFM95W.SCK

custom parts:
  Adafruit 4-channel I2C-safe Bi-directional Logic Level Converter: Because the Arduino (and Basic Stamp) are 5V devices, and most modern sensors, displays, flash cards and modes are 3.3V-only, many makers find that they need to perform level shifting/conversion to protect the 3.3V device from 5V. We do have some other handy level shifters in the shop, from the DIP 74LVC245 to the fancy bi-directional TXB0108. However, neither of these are happy to work with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
  Adafruit RFM9x LoRa Radio: Sending data over long distances is like magic, and now you can be a magician with this range of powerful and easy-to-use radio modules. Sure, sometimes you want to talk to a computer (a good time to use WiFi) or perhaps communicate with a Phone (choose Bluetooth Low Energy!) but what if you want to send data very far? Most WiFi, Bluetooth, Zigbee and other wireless chipsets use 2.4GHz, which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
